# Fritzing sketch ups (saved by Fritzing 0.9.2b)
circuit board: 9.05929cm x 8.57955cm
breadboards: 1

parts:
  Part1 = Arduino Nano (Rev3.0)
  Part2 = Power Cell LiPo Charger/Booster
  U2 = LIPO-2000mAh [package=lipo-2000]
  U1 = Switching step-up voltage regulator [package=sot23-5]
  R1 = Resistor [tolerance=±5% resistance=10k package=THT]
  X1 = USB Connectors [package=usb-a-s]
  Q1 = Basic FET P-Channel [package="D2Pak [SMD]"]
  C1 = Electrolytic Capacitor [capacitance=1000µF package="300 mil [THT, electrolytic]"]
  J1 = Power Jack [package=power_jack_pth_lock]
  D1 = Rectifier Diode [part_number=1N4001 package="300 mil [THT]"]
  U4 = ACS712 [package=so08]
  R2 = Resistor [tolerance=±5% resistance=10k package="1206 [SMD]"]
  R3 = Resistor [tolerance=±5% resistance=8.2k package="1206 [SMD]"]
  R4 = Resistor [tolerance=±5% resistance=8.2k package="1206 [SMD]"]

nets:
  GND: Part1.GND, Part2.GND, U2.-, U1.GND, R1.Pin_0, J1.GND, J1.GNDBREAK, U4.IP-, U4.GND, R4.Pin_0
  N1: Part1.D4, Part1.5V, Part2.5VIN, R1.Pin_1, Q1.drain, J1.PWR, D1.cathode
  N2: Part1.D5, Q1.Gate
  N3: Part1.A2, Q1.source, C1.+
  N4: Part1.A1, R2.Pin_0, R3.Pin_1
  N5: Part1.A0, U4.VOUT
  3V3: Part1.AREF, Part1.3V3, U4.VCC
  N6: Part2.VCC, U1.LX
  N7: Part2.VBATT, U2.+, R2.Pin_1
  N8: U1.OUT, D1.anode
  N9: X1.GND, C1.-, U4.IP+
  N10: R3.Pin_0, R4.Pin_1
